# Fritzing sketch schematics (saved by Fritzing 0.9.10b)
# 18650 Li-ion Battery: CC-BY Dr Kristofer Chan, King's College London/Remote-research.org

parts:
  Mod1 = Amica NodeMCU DEVKIT 1.0
  U1 = U.FL [package=u.fl]  # not connected
  Part1 = FTDI Basic Programmer
  R1 = PHOTOCELL [package=photocell]
  BAT1 = 18650 Li-ion Battery [package=battery-18650]
  MOD1 = MT3608 Boost No usb
  Part2 = Solar Panel [package="Renogy 50 Watts 12 Volt Monocrystalline Bendable Solar Panel"]
  TP1 = TP4056 [chip_label=TP4056 package="DIP (Dual Inline) [THT]"]
  R3 = Resistor [tolerance=±5% power=0.25 resistance=10k package=THT]
  ANT1 = Antenna  # not connected
  M1 = BME280

nets:
  N1: Mod1.pin1, Mod1.pin_10, Mod1.pin_26, Part1.POWER, R1.P$1, M1.VIN
  N2: Mod1.pin2, Mod1.pin_9, Mod1.pin_25, Mod1.pin_29, Part1.DTR, MOD1.IN_(-), MOD1.OUT_(-), TP1.pin6, R3.Pin_1, M1.GND
  N3: Mod1.pin3, Part1.RXI
  N4: Mod1.pin4, Part1.TXO
  N5: Mod1.pin_13, M1.SDA
  N6: Mod1.pin_14, M1.SCL
  N7: Mod1.pin_16, R1.P$2, R3.Pin_0
  N8: Mod1.pin_30, MOD1.OUT_(+)
  N9: BAT1.-, TP1.pin5
  N10: BAT1.+, TP1.pin4
  N11: MOD1.IN_(+), TP1.pin3
  N12: Part2.Connector_1, TP1.pin2
  N13: Part2.Connector_2, TP1.pin1

notes:
  TP4056
  MT3608
  FTDI
  BME280
  photoresistor
  U.FL socket

custom parts:
  18650 Li-ion Battery: 18650 li-ion Battery Standard 18650 battery with interactive connectors Creative Common Attribution 4.0 International (CC-BY 4.0) license. Any use of this part requires attribution of Dr Kristofer Chan, Department of Geography, King's College London. Contact kristofer.chan [at] kcl.ac.uk OR kris [at] remote-research.org for further information.
  MT3608 Boost No usb: Chip- MT3608 / B6289 DC to DC step up, power booster module. With adjustable output voltage. Current- 2A . || Input voltage- 2V-24V || Output voltage- 5V-28V Input interface- Inversed polarity- NO. || Led indicator- No.
  Solar Panel: Renogy 50 Watts 12 Volt Solar Panel
  TP4056: A DIP stand-in part for whatever IC you want. With 6 pins on a 300mil dual inline package (DIP) footprint.
  BME280: Temperature Humidity Barometric presure Sensor
